// Logisim project 8-1 Circuit.circ as structural Verilog: 1 circuit, main circuit main
module main (
  input  B,
  input  C,
  input  A,
  output F
);

  wire and_1_out, and_2_out, not_1_out;

  not not_1 (not_1_out, B);
  and and_1 (and_1_out, not_1_out, A);
  and and_2 (and_2_out, C, B, A);
  or or_1 (F, and_1_out, and_2_out);
endmodule
