// Logisim project 8-2 Circuit.circ as structural Verilog: 1 circuit, main circuit main
module main (
  input  a,
  input  b,
  input  z,
  output x,
  output y
);

  wire and_1_out, and_2_out, and_3_out, and_4_out, not_1_out, not_2_out;

  and and_1 (and_1_out, a, z);
  and and_2 (and_2_out, b, z);
  not not_1 (not_1_out, z);
  not not_2 (not_2_out, z);
  and and_3 (and_3_out, a, not_1_out);
  and and_4 (and_4_out, not_2_out, b);
  or or_1 (x, and_2_out, and_3_out);
  or or_2 (y, and_4_out, and_1_out);
endmodule
