// Logisim project INCREMENTER.circ as structural Verilog: 1 circuit, main circuit main
module main (
  input  A0,
  input  B0,
  input  A1,
  input  B1,
  input  A14,
  input  B14,
  input  A15,
  input  B15,
  input  MARInc,
  output OUT0,
  output OUT1,
  output OUT14,
  output OUT15
);

  wire and_1_out, and_2_out, and_3_out, and_4_out, and_5_out, and_6_out, or_1_out, or_2_out, or_3_out,
       xor_1_out, xor_3_out, xor_5_out, xor_7_out;

  xor xor_1 (xor_1_out, A0, B0);
  and and_1 (and_1_out, A0, MARInc);
  and and_2 (and_2_out, B0, MARInc);
  xor xor_2 (OUT0, xor_1_out, MARInc);
  or or_1 (or_1_out, and_1_out, and_2_out);
  xor xor_3 (xor_3_out, A1, B1);
  and and_3 (and_3_out, A1, or_1_out);
  and and_4 (and_4_out, B1, or_1_out);
  xor xor_4 (OUT1, xor_3_out, or_1_out);
  or or_2 (or_2_out, and_3_out, and_4_out);
  xor xor_5 (xor_5_out, A14, B14);
  and and_5 (and_5_out, A14, or_2_out);
  and and_6 (and_6_out, B14, or_2_out);
  xor xor_6 (OUT14, xor_5_out, or_2_out);
  or or_3 (or_3_out, and_5_out, and_6_out);
  xor xor_7 (xor_7_out, A15, B15);
  xor xor_8 (OUT15, xor_7_out, or_3_out);

  // Notes on the sheet:
  //   B15: pull=up
  //   (x12)
  //   ...
endmodule
